# Fritzing sketch hw2_1_fritz (saved by Fritzing 0.8.3b)
breadboards: 1

parts:
  S7 = Pushbutton [package="[THT]"]
  S8 = Pushbutton [package="[THT]"]
  S9 = Pushbutton [package="[THT]"]
  S10 = Pushbutton [package="[THT]"]
  S11 = Pushbutton [package="[THT]"]
  S12 = Pushbutton [package="[THT]"]
  Boarduino2 = Boarduino DC v3
  S13 = Pushbutton [package="[THT]"]
  S14 = Pushbutton [package="[THT]"]
  S15 = Pushbutton [package="[THT]"]

nets:
  N1: S7.Pin_1, Boarduino2.D7
  N2: S7.Pin_3, S7.Pin_4, S8.Pin_3, S8.Pin_4, S9.Pin_1, S9.Pin_2, S10.Pin_1, S10.Pin_2, S11.Pin_1, S11.Pin_2, S12.Pin_3, S12.Pin_4, Boarduino2.GND, S13.Pin_1, S13.Pin_2, S14.Pin_3, S14.Pin_4, S15.Pin_3, S15.Pin_4
  N3: S8.Pin_1, Boarduino2.D6
  N4: S9.Pin_3, Boarduino2.D5
  N5: S10.Pin_3, Boarduino2.D8
  N6: S11.Pin_3, Boarduino2.D10
  N7: S12.Pin_1, Boarduino2.D9
  N8: Boarduino2.D2, S13.Pin_4
  N9: Boarduino2.D3, S14.Pin_1, S14.Pin_2
  N10: Boarduino2.D4, S15.Pin_1, S15.Pin_2

notes:
  Front
  ABC DEF GHI
  JKL MNO PQR
  STU VWX YZ_
  Right
  Top
