# Fritzing sketch hw2_fritz (saved by Fritzing 0.8.3b)
breadboards: 1

parts:
  S1 = Pushbutton [package="[THT]"]
  S2 = Pushbutton [package="[THT]"]
  S3 = Pushbutton [package="[THT]"]
  S4 = Pushbutton [package="[THT]"]
  S5 = Pushbutton [package="[THT]"]
  S6 = Pushbutton [package="[THT]"]
  Boarduino1 = Boarduino DC v3

nets:
  N1: S1.Pin_1, S1.Pin_2, Boarduino1.D2
  N2: S1.Pin_3, S1.Pin_4, S2.Pin_3, S2.Pin_4, S3.Pin_3, S3.Pin_4, S4.Pin_3, S4.Pin_4, S5.Pin_3, S5.Pin_4, S6.Pin_3, S6.Pin_4, Boarduino1.GND
  N3: S2.Pin_1, S2.Pin_2, Boarduino1.D3
  N4: S3.Pin_1, S3.Pin_2, Boarduino1.D4
  N5: S4.Pin_1, S4.Pin_2, Boarduino1.D5
  N6: S5.Pin_1, S5.Pin_2, Boarduino1.D6
  N7: S6.Pin_1, S6.Pin_2, Boarduino1.D7
