# Fritzing sketch hw3_fritz (saved by Fritzing 0.8.3b)
breadboards: 1

parts:
  Boarduino2 = Boarduino DC v3
  J1 = Basic Force Sensing Resistor (FSR) [package=THT]
  S1 = Momentary Switch [package=ksa_sealed_tac_switch]
  S2 = Round Pushbutton
  R1 = Resistor [package="2010 [SMD]"]
  R2 = Resistor [package="2010 [SMD]"]
  Part1 = LilyPad Accelerometer ADXL335
  R3 = Resistor [package="2010 [SMD]"]

nets:
  N1: Boarduino2.GND, S1.3, S2.leg0, Part1.COM, R3.Pin_1
  N2: Boarduino2.D2, S2.leg1
  N3: Boarduino2.D3, S1.1
  N4: Boarduino2.D8, R1.Pin_1, R2.Pin_1
  N5: Boarduino2.D9, R2.Pin_0
  N6: Boarduino2.D10, R1.Pin_0
  N7: Boarduino2.A1, Part1.XOUT
  N8: Boarduino2.A0, J1.pin_0, R3.Pin_0
  +5V: Boarduino2.+5V, J1.pin_1, Part1.5V

notes:
  Steering Wheel
  Foot Pedal
  Headphones
  Left Foil
  Right Foil
  10M ohm
  20K ohm
